// Logisim project oaclab2.circ as structural Verilog: 4 circuits, main circuit alu16bit
module mini_alu (
  input  InvertInput1,
  input  Input1,
  input  Selector1,
  input  Selector0,
  input  InvertInput2,
  input  Less,
  input  Input2,
  input  Cin,
  output Result,
  output Set,
  output Cout
);

  wire and_1_out, multiplexer_1_out, multiplexer_2_out, not_1_out, not_2_out, or_1_out;

  Multiplexer multiplexer_1 (.in0(Input1), .in1(not_1_out), .out(multiplexer_1_out), .sel(InvertInput1));  // open: en
  not not_1 (not_1_out, Input1);
  Multiplexer multiplexer_2 (.in0(Input2), .in1(not_2_out), .out(multiplexer_2_out), .sel(InvertInput2));  // open: en
  not not_2 (not_2_out, Input2);
  and and_1 (and_1_out, multiplexer_1_out, multiplexer_2_out);
  or or_1 (or_1_out, multiplexer_1_out, multiplexer_2_out);
  Adder #(.width(1)) adder_1 (.a(multiplexer_1_out), .b(multiplexer_2_out), .out(Set), .cin(Cin), .cout(Cout));
  Multiplexer #(.select(2)) multiplexer_3 (
    .in0(and_1_out), .in1(or_1_out), .in2(Set), .in3(Less), .out(Result), .sel({Selector1, Selector0}));  // open: en
endmodule

module alu32bit (
  input  InvertInput1,
  input  InvertInput2,
  input  Selector1,
  input  Selector0,
  input  Input1_0,
  input  Input1_1,
  input  Input1_2,
  input  Input1_3,
  input  Input2_0,
  input  Input2_1,
  input  Input2_2,
  input  Input2_3,
  input  Input1_4,
  input  Input1_5,
  input  Input1_6,
  input  Input1_7,
  input  Input2_4,
  input  Input2_5,
  input  Input2_6,
  input  Input2_7,
  input  Input1_8,
  input  Input1_9,
  input  Input1_10,
  input  Input1_11,
  input  Input2_8,
  input  Input2_9,
  input  Input2_10,
  input  Input2_11,
  input  Input1_12,
  input  Input1_13,
  input  Input1_14,
  input  Input1_15,
  input  Input2_12,
  input  Input2_13,
  input  Input2_14,
  input  Input2_15,
  input  Input1_16,
  input  Input1_17,
  input  Input1_18,
  input  Input1_19,
  input  Input2_16,
  input  Input2_17,
  input  Input2_18,
  input  Input2_19,
  input  Input1_20,
  input  Input1_21,
  input  Input1_22,
  input  Input1_23,
  input  Input2_20,
  input  Input2_21,
  input  Input2_22,
  input  Input2_23,
  input  Input1_24,
  input  Input1_25,
  input  Input1_26,
  input  Input1_27,
  input  Input2_24,
  input  Input2_25,
  input  Input2_26,
  input  Input2_27,
  input  Input1_28,
  input  Input1_29,
  input  Input1_30,
  input  Input1_31,
  input  Input2_28,
  input  Input2_29,
  input  Input2_30,
  input  Input2_31,
  output Result0,
  output Result1,
  output Result2,
  output Result3,
  output Result4,
  output Result5,
  output Result6,
  output Result7,
  output Result8,
  output Result9,
  output Result10,
  output Result11,
  output Result12,
  output Result13,
  output Result14,
  output Bne,
  output Result15,
  output Result16,
  output Result17,
  output Result18,
  output Result19,
  output Result20,
  output Result21,
  output Result22,
  output Result23,
  output Result24,
  output Result25,
  output Result26,
  output Result27,
  output Result28,
  output Result29,
  output Cout,
  output Result30,
  output Result31
);

  wire alu16bit_1_bne, alu16bit_1_cout, alu16bit_2_bne, not_1_out, not_2_out, or_1_out;

  alu16bit alu16bit_1 (
    .Input1_0(Input1_0), .Input1_1(Input1_1), .Input1_2(Input1_2), .Input1_3(Input1_3), .Input2_0(Input2_0),
    .Input2_1(Input2_1), .Input2_2(Input2_2), .Input2_3(Input2_3), .Input1_4(Input1_4), .Input1_5(Input1_5),
    .Input1_6(Input1_6), .Input1_7(Input1_7), .Input2_4(Input2_4), .Input2_5(Input2_5), .Input2_6(Input2_6),
    .Input2_7(Input2_7), .Input1_8(Input1_8), .Input1_9(Input1_9), .Input1_10(Input1_10),
    .Input1_11(Input1_11), .Input2_8(Input2_8), .Input2_9(Input2_9), .Input2_10(Input2_10),
    .Input2_11(Input2_11), .Input1_12(Input1_12), .Input1_13(Input1_13), .Input1_14(Input1_14),
    .Input1_15(Input1_15), .Input2_12(Input2_12), .Input2_13(Input2_13), .Input2_14(Input2_14),
    .Input2_15(Input2_15), .InvertInput1(InvertInput1), .InvertInput2(InvertInput2), .Cin(InvertInput2),
    .Selector1(Selector1), .Selector0(Selector0), .Cout(alu16bit_1_cout), .Result0(Result0),
    .Result1(Result1), .Result2(Result2), .Result3(Result3), .Result4(Result4), .Result5(Result5),
    .Bne(alu16bit_1_bne), .Result6(Result6), .Result7(Result7), .Result8(Result8), .Result9(Result9),
    .Result10(Result10), .Result11(Result11), .Result12(Result12), .Result13(Result13), .Result14(Result14),
    .Result15(Result15));
  alu16bit alu16bit_2 (
    .Input1_0(Input1_16), .Input1_1(Input1_17), .Input1_2(Input1_18), .Input1_3(Input1_19),
    .Input2_0(Input2_16), .Input2_1(Input2_17), .Input2_2(Input2_18), .Input2_3(Input2_19),
    .Input1_4(Input1_20), .Input1_5(Input1_21), .Input1_6(Input1_22), .Input1_7(Input1_23),
    .Input2_4(Input2_20), .Input2_5(Input2_21), .Input2_6(Input2_22), .Input2_7(Input2_23),
    .Input1_8(Input1_24), .Input1_9(Input1_25), .Input1_10(Input1_26), .Input1_11(Input1_27),
    .Input2_8(Input2_24), .Input2_9(Input2_25), .Input2_10(Input2_26), .Input2_11(Input2_27),
    .Input1_12(Input1_28), .Input1_13(Input1_29), .Input1_14(Input1_30), .Input1_15(Input1_31),
    .Input2_12(Input2_28), .Input2_13(Input2_29), .Input2_14(Input2_30), .Input2_15(Input2_31),
    .InvertInput1(InvertInput1), .InvertInput2(InvertInput2), .Cin(alu16bit_1_cout), .Selector1(Selector1),
    .Selector0(Selector0), .Cout(Cout), .Result0(Result16), .Result1(Result17), .Result2(Result18),
    .Result3(Result19), .Result4(Result20), .Result5(Result21), .Bne(alu16bit_2_bne), .Result6(Result22),
    .Result7(Result23), .Result8(Result24), .Result9(Result25), .Result10(Result26), .Result11(Result27),
    .Result12(Result28), .Result13(Result29), .Result14(Result30), .Result15(Result31));
  not not_1 (not_1_out, alu16bit_1_bne);
  not not_2 (not_2_out, alu16bit_2_bne);
  or or_1 (or_1_out, not_1_out, not_2_out);
  not not_3 (Bne, or_1_out);

  // Notes on the sheet:
  //   Aqui uso Cin = InvertInput2 para economizar bit, já que não vou usar como módulo
endmodule

module alu4bit (
  input  InvertInput1,
  input  InvertInput2,
  input  Selector1,
  input  Selector0,
  input  Cin,
  input  Input1_0,
  input  Input2_0,
  input  Input1_1,
  input  Input2_1,
  input  Input1_2,
  input  Input2_2,
  input  Input1_3,
  input  Input2_3,
  output Result0,
  output Result1,
  output Bne,
  output Result2,
  output Result3,
  output Cout
);

  wire mini_alu_1_cout, mini_alu_2_cout, mini_alu_3_cout, mini_alu_4_set, or_1_out;

  mini_alu mini_alu_1 (
    .Input1(Input1_0), .Input2(Input2_0), .InvertInput1(InvertInput1), .InvertInput2(InvertInput2),
    .Cin(Cin), .Selector1(Selector1), .Selector0(Selector0), .Cout(mini_alu_1_cout), .Less(mini_alu_4_set),
    .Result(Result0));  // open: Set
  mini_alu mini_alu_2 (
    .Input1(Input1_1), .Input2(Input2_1), .InvertInput1(InvertInput1), .InvertInput2(InvertInput2),
    .Cin(mini_alu_1_cout), .Selector1(Selector1), .Selector0(Selector0), .Cout(mini_alu_2_cout),
    .Result(Result1));  // open: Less, Set
  mini_alu mini_alu_3 (
    .Input1(Input1_2), .Input2(Input2_2), .InvertInput1(InvertInput1), .InvertInput2(InvertInput2),
    .Cin(mini_alu_2_cout), .Selector1(Selector1), .Selector0(Selector0), .Cout(mini_alu_3_cout),
    .Result(Result2));  // open: Less, Set
  mini_alu mini_alu_4 (
    .Input1(Input1_3), .Input2(Input2_3), .InvertInput1(InvertInput1), .InvertInput2(InvertInput2),
    .Cin(mini_alu_3_cout), .Selector1(Selector1), .Selector0(Selector0), .Cout(Cout), .Result(Result3),
    .Set(mini_alu_4_set));  // open: Less
  or or_1 (or_1_out, Result0, Result1, Result2, Result3);
  not not_1 (Bne, or_1_out);

  // Notes on the sheet:
  //   Aqui preciso de Cin para modularizar o negócio todo
endmodule

module alu16bit (
  input  InvertInput1,
  input  InvertInput2,
  input  Cin,
  input  Selector1,
  input  Selector0,
  input  Input1_0,
  input  Input1_1,
  input  Input1_2,
  input  Input1_3,
  input  Input2_0,
  input  Input2_1,
  input  Input2_2,
  input  Input2_3,
  input  Input1_4,
  input  Input1_5,
  input  Input1_6,
  input  Input1_7,
  input  Input2_4,
  input  Input2_5,
  input  Input2_6,
  input  Input2_7,
  input  Input1_8,
  input  Input1_9,
  input  Input1_10,
  input  Input1_11,
  input  Input2_8,
  input  Input2_9,
  input  Input2_10,
  input  Input2_11,
  input  Input1_12,
  input  Input1_13,
  input  Input1_14,
  input  Input1_15,
  input  Input2_12,
  input  Input2_13,
  input  Input2_14,
  input  Input2_15,
  output Result0,
  output Result1,
  output Result2,
  output Result3,
  output Result4,
  output Result5,
  output Bne,
  output Result6,
  output Result7,
  output Result8,
  output Result9,
  output Result10,
  output Result11,
  output Result12,
  output Result13,
  output Result14,
  output Cout,
  output Result15
);

  wire alu4bit_1_bne, alu4bit_1_cout, alu4bit_2_bne, alu4bit_2_cout, alu4bit_3_bne, alu4bit_3_cout,
       alu4bit_4_bne, not_1_out, not_2_out, not_3_out, not_4_out, or_1_out, or_2_out, or_3_out;

  alu4bit alu4bit_1 (
    .Input1_0(Input1_0), .Input2_0(Input2_0), .Input1_1(Input1_1), .Input2_1(Input2_1), .Input1_2(Input1_2),
    .Input2_2(Input2_2), .Input1_3(Input1_3), .Input2_3(Input2_3), .InvertInput1(InvertInput1),
    .InvertInput2(InvertInput2), .Cin(Cin), .Selector1(Selector1), .Selector0(Selector0), .Result0(Result0),
    .Result1(Result1), .Bne(alu4bit_1_bne), .Result2(Result2), .Result3(Result3), .Cout(alu4bit_1_cout));
  alu4bit alu4bit_2 (
    .Input1_0(Input1_4), .Input2_0(Input2_4), .Input1_1(Input1_5), .Input2_1(Input2_5), .Input1_2(Input1_6),
    .Input2_2(Input2_6), .Input1_3(Input1_7), .Input2_3(Input2_7), .InvertInput1(InvertInput1),
    .InvertInput2(InvertInput2), .Cin(alu4bit_1_cout), .Selector1(Selector1), .Selector0(Selector0),
    .Result0(Result4), .Result1(Result5), .Bne(alu4bit_2_bne), .Result2(Result6), .Result3(Result7),
    .Cout(alu4bit_2_cout));
  alu4bit alu4bit_3 (
    .Input1_0(Input1_8), .Input2_0(Input2_8), .Input1_1(Input1_9), .Input2_1(Input2_9), .Input1_2(Input1_10),
    .Input2_2(Input2_10), .Input1_3(Input1_11), .Input2_3(Input2_11), .InvertInput1(InvertInput1),
    .InvertInput2(InvertInput2), .Cin(alu4bit_2_cout), .Selector1(Selector1), .Selector0(Selector0),
    .Result0(Result8), .Result1(Result9), .Bne(alu4bit_3_bne), .Result2(Result10), .Result3(Result11),
    .Cout(alu4bit_3_cout));
  alu4bit alu4bit_4 (
    .Input1_0(Input1_12), .Input2_0(Input2_12), .Input1_1(Input1_13), .Input2_1(Input2_13),
    .Input1_2(Input1_14), .Input2_2(Input2_14), .Input1_3(Input1_15), .Input2_3(Input2_15),
    .InvertInput1(InvertInput1), .InvertInput2(InvertInput2), .Cin(alu4bit_3_cout), .Selector1(Selector1),
    .Selector0(Selector0), .Result0(Result12), .Result1(Result13), .Bne(alu4bit_4_bne), .Result2(Result14),
    .Result3(Result15), .Cout(Cout));
  not not_1 (not_1_out, alu4bit_1_bne);
  not not_2 (not_2_out, alu4bit_2_bne);
  not not_3 (not_3_out, alu4bit_3_bne);
  not not_4 (not_4_out, alu4bit_4_bne);
  or or_1 (or_1_out, not_1_out, not_2_out);
  or or_2 (or_2_out, not_3_out, not_4_out);
  or or_3 (or_3_out, or_1_out, or_2_out);
  not not_5 (Bne, or_3_out);

  // Notes on the sheet:
  //   Aqui preciso de Cin para modularizar o negócio todo
endmodule
